# Fritzing sketch schematic (saved by Fritzing 0.9.6b)
perfboards: 3

parts:
  Mod1 = Raspberry Pi Pico
  S1 = Pushbutton [package="[THT]"]
  S2 = Pushbutton [package="[THT]"]
  S3 = Pushbutton [package="[THT]"]
  S4 = Pushbutton [package="[THT]"]
  S5 = Pushbutton [package="[THT]"]
  S6 = Pushbutton [package="[THT]"]
  S7 = Pushbutton [package="[THT]"]
  S8 = Pushbutton [package="[THT]"]
  S9 = Pushbutton [package="[THT]"]
  S10 = Pushbutton [package="[THT]"]
  S11 = Pushbutton [package="[THT]"]
  S12 = Pushbutton [package="[THT]"]
  S13 = Pushbutton [package="[THT]"]
  VCC1 = Battery
  U1 = SWITCH_SPDT [package=kps-1290]
  R1 = Resistor [tolerance=±5% resistance=270 package="0805 [SMD]"]
  C1 = Ceramic Capacitor [capacitance=100nF voltage=35V package="200 mil [THT, multilayer]"]
  S15 = Pushbutton [package="[SMD]"]
  S16 = Pushbutton [package="[SMD]"]
  S17 = Pushbutton [package="[THT]"]
  S18 = Pushbutton [package="[THT]"]
  S19 = Pushbutton [package="[THT]"]
  S21 = Pushbutton [package="[THT]"]
  S22 = Pushbutton [package="[THT]"]
  S14 = Pushbutton [package="[SMD]"]
  LED2 = smd LED [color="Blue (430nm)" package="0805 [SMD]"]  # not connected
  U5 = 3.5mm Audio Jack [package=audio-jack-3.5mm-smd]

nets:
  N1: Mod1.pin_1, R1.Pin_1
  N2: Mod1.pin_3, Mod1.pin_8, Mod1.pin_13, Mod1.pin_18, Mod1.pin_23, Mod1.pin_28, Mod1.pin_33, Mod1.pin_38, Mod1.pin_42, VCC1.-, C1.0, U5.LEFT
  N3: Mod1.pin_39, U1.P
  N4: S1.Pin_1, S1.Pin_2
  N5: S1.Pin_3, S1.Pin_4
  N6: S2.Pin_1, S2.Pin_2
  N7: S2.Pin_3, S2.Pin_4
  N8: S3.Pin_1, S3.Pin_2
  N9: S3.Pin_3, S3.Pin_4
  N10: S4.Pin_1, S4.Pin_2
  N11: S4.Pin_3, S4.Pin_4
  N12: S5.Pin_1, S5.Pin_2
  N13: S5.Pin_3, S5.Pin_4
  N14: S6.Pin_1, S6.Pin_2
  N15: S6.Pin_3, S6.Pin_4
  N16: S7.Pin_1, S7.Pin_2
  N17: S7.Pin_3, S7.Pin_4
  N18: S8.Pin_1, S8.Pin_2
  N19: S8.Pin_3, S8.Pin_4
  N20: S9.Pin_1, S9.Pin_2
  N21: S9.Pin_3, S9.Pin_4
  N22: S10.Pin_1, S10.Pin_2
  N23: S10.Pin_3, S10.Pin_4
  N24: S11.Pin_1, S11.Pin_2
  N25: S11.Pin_3, S11.Pin_4
  N26: S12.Pin_1, S12.Pin_2
  N27: S12.Pin_3, S12.Pin_4
  N28: S13.Pin_1, S13.Pin_2
  N29: S13.Pin_3, S13.Pin_4
  N30: VCC1.+, U1.O
  N31: R1.Pin_0, C1.1, U5.SLEEVE
  N32: S15.Pin_1, S15.Pin_2
  N33: S15.Pin_3, S15.Pin_4
  N34: S16.Pin_1, S16.Pin_2
  N35: S16.Pin_3, S16.Pin_4
  N36: S17.Pin_1, S17.Pin_2
  N37: S17.Pin_3, S17.Pin_4
  N38: S18.Pin_1, S18.Pin_2
  N39: S18.Pin_3, S18.Pin_4
  N40: S19.Pin_1, S19.Pin_2
  N41: S19.Pin_3, S19.Pin_4
  N42: S21.Pin_1, S21.Pin_2
  N43: S21.Pin_3, S21.Pin_4
  N44: S22.Pin_1, S22.Pin_2
  N45: S22.Pin_3, S22.Pin_4
  N46: S14.Pin_1, S14.Pin_2
  N47: S14.Pin_3, S14.Pin_4

notes:
  Клавиатура
  Выбор октавы
  Выбор режимов сигнала

custom parts:
  Raspberry Pi Pico: Raspberry Pi Pico. Based around the RP2040 microcontroller the Pico is a low cost microcontroller device bringing Raspberry Pi quality, cost, and easy of use to the microcontroller space. Jan 2021, Split part in to two versions: tht (this one) and SMD. This one will drill holes for a .1 in header in pcb to allow plugging in the module as well as providing pads to solder the module to the top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
